# Fritzing sketch GreenChristmasGift (saved by Fritzing 0.7.10b)

parts:
  Arduino1 = Arduino
  Q1 = NPN-Transistor [package="TO92 [THT]"]
  Q2 = NPN-Transistor [package="TO92 [THT]"]
  D1 = Rectifier Diode [part_number=1N4001 package="300 mil [THT]"]
  D2 = Rectifier Diode [part_number=1N4001 package="300 mil [THT]"]
  R1 = Resistor [tolerance=±5% resistance=220 package=THT]
  R2 = Resistor [tolerance=±5% resistance=220 package=THT]
  M1 = DC Motor
  M2 = DC Motor
  J1 = Piezo Speaker
  LED1 = LED - 5mm [color="Red (633nm)" package="5 mm [THT]"]
  R3 = Resistor [tolerance=±5% resistance=1k package=THT]
  R4 = Resistor [tolerance=±5% resistance=1k package=THT]
  LED2 = LED - 5mm [color="Red (633nm)" package="5 mm [THT]"]
  LED3 = LED - 5mm [color="Red (633nm)" package="5 mm [THT]"]
  R5 = Resistor [tolerance=±5% resistance=1k package=THT]
  R6 = Photocell (LDR) [package=THT]
  R7 = Resistor [tolerance=±5% resistance=220 package=THT]

nets:
  GND: Arduino1.GND, Q1.E, Q2.E, J1.pin2, LED1.cathode, LED2.cathode, LED3.cathode, R7.Pin_1
  N1: Arduino1.D11, J1.pin1
  N2: Arduino1.D10, R3.Pin_1
  N3: Arduino1.D9, R4.Pin_1
  N4: Arduino1.D6, R5.Pin_1
  N5: Arduino1.D5, R2.Pin_0
  N6: Arduino1.D3, R1.Pin_1
  5V: Arduino1.+5V, D1.cathode, D2.cathode, M1.pin_2, M2.pin_2, R6.pin_0
  N7: Arduino1.A0, R6.pin_1, R7.Pin_0
  N8: Q1.B, R1.Pin_0
  N9: Q1.C, D1.anode, M1.pin_1
  N10: Q2.B, R2.Pin_1
  N11: Q2.C, D2.anode, M2.pin_1
  N12: LED1.anode, R3.Pin_0
  N13: R4.Pin_0, LED2.anode
  N14: LED3.anode, R5.Pin_0

notes:
  Need to add some jumpers for night/dark config
